// Logisim project FullAdder_Mackin.circ as structural Verilog: 1 circuit, main circuit main
module main (
  input  A,
  input  B,
  input  Cin
);

  wire and_1_out, and_2_out, or_1_out, xor_1_out, xor_2_out;

  xor xor_1 (xor_1_out, A, B);
  and and_1 (and_1_out, xor_1_out, Cin);
  and and_2 (and_2_out, B, A);
  xor xor_2 (xor_2_out, xor_1_out, Cin);
  or or_1 (or_1_out, and_1_out, and_2_out);
  LED led_1 (.in(xor_2_out));
  LED led_2 (.in(or_1_out));

  // Notes on the sheet:
  //   Sum
  //   Count
endmodule
