// Logisim project HalfAdderandGates.circ as structural Verilog: 1 circuit, main circuit main
module main (
  input  in_1,
  input  in_2,
  input  in_3,
  input  in_4,
  input  in_5,
  input  in_6,
  input  in_7,
  output NOT,
  output S,
  output AND,
  output C,
  output OR
);

  wire nand_1_out, nand_2_out, nand_3_out, nand_7_out, nand_8_out, nand_9_out;

  nand nand_1 (nand_1_out, in_2, in_4);
  nand nand_2 (nand_2_out, in_6, in_6);
  nand nand_3 (nand_3_out, in_7, in_7);
  nand nand_4 (NOT, in_1, in_1);
  nand nand_5 (AND, nand_1_out, nand_1_out);
  nand nand_6 (OR, nand_2_out, nand_3_out);
  nand nand_7 (nand_7_out, in_3, in_5);
  nand nand_8 (nand_8_out, in_3, nand_7_out);
  nand nand_9 (nand_9_out, nand_7_out, in_5);
  nand nand_10 (S, nand_8_out, nand_9_out);
  nand nand_11 (C, nand_7_out, nand_7_out);

  // Notes on the sheet:
  //   Half Adder
endmodule
