// Logisim project SRandTypeD-latches.circ as structural Verilog: 1 circuit, main circuit main
module main (
  input  S,
  input  R,
  input  D,
  input  Remember,
  output Q,
  output nQ,
  output Q_2,
  output nQ_2
);

  wire nand_1_out, nand_2_out, not_1_out;

  not not_1 (not_1_out, D);
  nand nand_1 (nand_1_out, D, Remember);
  nand nand_2 (nand_2_out, Remember, not_1_out);
  nand nand_3 (Q, S, nQ);
  nand nand_4 (nQ, Q, R);
  nand nand_5 (Q_2, nand_1_out, nQ_2);
  nand nand_6 (nQ_2, Q_2, nand_2_out);

  // Notes on the sheet:
  //   SR latch
  //   Type-D latch
endmodule
